// Digital circuit lc3.dig as structural Verilog
module lc3 (
  input  Clk
);

  wire ADDR1MUX, ALUK, and_1_out, and_2_out, and_3_out, BEN, GateALU, GateMARMUX, GateMDR, GatePC,
       lc3_cc_logic_1_n, lc3_cc_logic_1_p, lc3_cc_logic_1_z, LD_BEN, LD_CC, LD_IR, LD_MAR, LD_MDR, LD_PC,
       LD_REG, MARMUX, MIO_EN, N, or_1_out, P, R, R_W, SR2MUX, Z;
  wire [1:0] ADDR2MUX, PCMUX, SR1MUX;
  wire [2:0] DR, multiplexer_6_out, SR1;
  wire [4:0] Immed;
  wire [4:1] IR_15_11;
  wire [15:0] D_in, D_out, driver_1_out, lc3_alu_1_alu, lc3_alu_2_p10, lc3_memory_1_p7,
       lc3_register_file_1_sr2_out, multiplexer_1_out, multiplexer_2_out, multiplexer_3_out,
       multiplexer_4_out, multiplexer_5_out, PC, plus_1_s, SEXT_2_out, SEXT_3_out, SEXT_4_out, SEXT_out,
       SR1_OUT;

  Register #(.Bits(16)) IR (.D(driver_1_out), .C(Clk), .en(LD_IR), .Q({IR_15_11, DR, SR1, SR2MUX, Immed}));
  BitExtender #(.inputBits(11)) SEXT (.in({DR[1:0], SR1, SR2MUX, Immed}), .out(SEXT_out));
  BitExtender #(.inputBits(9)) SEXT_2 (.in({SR1, SR2MUX, Immed}), .out(SEXT_2_out));
  BitExtender #(.inputBits(6)) SEXT_3 (.in({SR2MUX, Immed}), .out(SEXT_3_out));
  assign driver_1_out = GateMARMUX ? multiplexer_1_out : 16'bz;  // Driver driver_1
  Multiplexer #(.Bits(16)) multiplexer_1 (
    .sel(MARMUX), .in_0({{8{1'b0}}, SR1[1:0], SR2MUX, Immed}), .in_1(lc3_alu_1_alu), .out(multiplexer_1_out));
  Multiplexer #(.Selector_Bits(2), .Bits(16)) multiplexer_2 (
    .sel(ADDR2MUX), .in_0({16{1'b0}}), .in_1(SEXT_out), .in_2(SEXT_2_out), .in_3(SEXT_3_out),
    .out(multiplexer_2_out));
  Multiplexer #(.Bits(16)) multiplexer_3 (.sel(ADDR1MUX), .in_0(PC), .in_1(SR1_OUT), .out(multiplexer_3_out));
  LED u_N (.in(N));
  Register N_2 (.D(lc3_cc_logic_1_n), .C(Clk), .en(LD_CC), .Q(N));
  lc3_alu lc3_alu_1 (.ALU(lc3_alu_1_alu), .A(multiplexer_2_out), .B(multiplexer_3_out), .ALUK(2'b00));
  Register u_Z (.D(lc3_cc_logic_1_z), .C(Clk), .en(LD_CC), .Q(Z));
  lc3_cc_logic lc3_cc_logic_1 (.D_in(driver_1_out), .N(lc3_cc_logic_1_n), .Z(lc3_cc_logic_1_z), .P(lc3_cc_logic_1_p));
  LED Z_2 (.in(Z));
  LED u_P (.in(P));
  Register P_2 (.D(lc3_cc_logic_1_p), .C(Clk), .en(LD_CC), .Q(P));
  // lc3_control lc3_control_1: pin names not known; wires that end beside it: LD_MAR, Clk, LD_MDR, 1'b0, LD_IR, R, LD_BEN, {IR_15_11, DR[2]}, LD_REG, BEN, LD_CC, 1'b1, LD_PC, 1'b0, GatePC, GateMDR, GateALU, GateMARMUX, PCMUX
  assign driver_1_out = GateMDR ? D_in : 16'bz;  // Driver driver_2
  Register #(.Bits(16)) MDR (.D(D_out), .C(Clk), .en(LD_MDR), .Q(D_in));
  Add #(.Bits(16)) plus_1 (.a(PC), .b(16'h1), .c_i(1'b0), .s(plus_1_s));  // open: c_o
  // lc3_memory lc3_memory_1: pin names not known; wires that end beside it: R, D_out, Clk, R_W, MIO_EN, D_in, lc3_memory_1_p7
  Register #(.Bits(16), .isProgramCounter("true")) u_PC (.D(multiplexer_4_out), .C(Clk), .en(LD_PC), .Q(PC));
  Multiplexer #(.Selector_Bits(2), .Bits(16)) multiplexer_4 (
    .sel(PCMUX), .in_0(plus_1_s), .in_1(lc3_alu_1_alu), .in_2(driver_1_out), .in_3({16{1'b0}}),
    .out(multiplexer_4_out));
  assign driver_1_out = GatePC ? PC : 16'bz;  // Driver driver_3
  Register #(.Bits(16)) MAR (.D(driver_1_out), .C(Clk), .en(LD_MAR), .Q(lc3_memory_1_p7));
  BitExtender #(.inputBits(5)) SEXT_4 (.in(Immed), .out(SEXT_4_out));
  Register u_BEN (.D(or_1_out), .C(Clk), .en(LD_BEN), .Q(BEN));
  lc3_register_file lc3_register_file_1 (
    .Clk(Clk), .Data(driver_1_out), .LD_Reg(LD_REG), .DR(DR), .SR1(multiplexer_6_out), .SR2(Immed[2:0]),
    .SR2_OUT(lc3_register_file_1_sr2_out), .SR1_OUT(SR1_OUT));
  Multiplexer #(.Bits(16)) multiplexer_5 (
    .sel(SR2MUX), .in_0(lc3_register_file_1_sr2_out), .in_1(SEXT_4_out), .out(multiplexer_5_out));
  // lc3_alu lc3_alu_2: pin names not known; wires that end beside it: SR1MUX, ADDR2MUX, ALUK, ADDR1MUX, MARMUX, MIO_EN, R_W, ALUK, multiplexer_5_out, lc3_alu_2_p10, SR1_OUT
  or or_1 (or_1_out, and_3_out, and_2_out, and_1_out);
  assign driver_1_out = GateALU ? lc3_alu_2_p10 : 16'bz;  // Driver driver_4
  and and_1 (and_1_out, DR[2], N);
  and and_2 (and_2_out, DR[1], Z);
  and and_3 (and_3_out, DR[0], P);
  Multiplexer #(.Selector_Bits(2), .Bits(3)) multiplexer_6 (
    .sel(SR1MUX), .in_0(SR1), .in_1(DR), .in_2(3'b110), .in_3(3'b000), .out(multiplexer_6_out));

  // Other names for the same wires on the sheet: SR2[2:0] = Immed[2:0]; IR_15_11[0] = DR[2]
endmodule
